// Digital circuit 6bit_and.dig as structural Verilog
module _6bit_and (
  input  [5:0] A_6,
  input  [5:0] B_6,
  output Out
);

  wire _3bit_and_1_out, _3bit_and_2_out;

  _3Bit_and _3bit_and_1 (.A_3(A_6[2:0]), .B_3(B_6[2:0]), .Out(_3bit_and_1_out));
  _3Bit_and _3bit_and_2 (.A_3(A_6[5:3]), .B_3(B_6[5:3]), .Out(_3bit_and_2_out));
  and and_1 (Out, _3bit_and_1_out, _3bit_and_2_out);
endmodule
